# Fritzing sketch blink1 (saved by Fritzing 0.9.3b)
breadboards: 1

parts:
  저항1 = Resistor [tolerance=±5% resistance=220 package=THT]
  Part1 = Arduino Uno (Rev3) - ICSP
  LED3 = LED - 5mm [color="Red (633nm)" package="5 mm [THT]"]

nets:
  N1: 저항1.Pin_0, Part1.D13/SCK
  N2: 저항1.Pin_1, LED3.anode
  N3: Part1.GND, LED3.cathode

notes:
  LED +
  LED -
