# Fritzing sketch blink3 (saved by Fritzing 0.9.3b)
breadboards: 1

parts:
  R1 = Resistor [tolerance=±5% resistance=220 package=THT]
  R2 = Resistor [tolerance=±5% resistance=220 package=THT]
  저항1 = Resistor [tolerance=±5% resistance=220 package=THT]
  Part1 = Arduino Uno (Rev3) - ICSP
  LED3 = LED - 5mm [color="Red (633nm)" package="5 mm [THT]"]
  LED4 = LED - 5mm [color="Orange (605nm)" package="5 mm [THT]"]
  LED5 = LED - 5mm [color="Green (555nm)" package="5 mm [THT]"]

nets:
  N1: R1.Pin_0, Part1.D11_PWM/MOSI
  N2: R1.Pin_1, LED5.anode
  N3: R2.Pin_0, Part1.D12/MISO
  N4: R2.Pin_1, LED4.anode
  N5: 저항1.Pin_0, Part1.D13/SCK
  N6: 저항1.Pin_1, LED3.anode
  N7: Part1.GND, LED3.cathode, LED4.cathode

notes:
  LED +
  LED -
  D11
  D12
  D13
