# Fritzing sketch dust_keypad (saved by Fritzing 0.9.3b)
breadboards: 1

parts:
  Part2 = LCD Keypad Shield
  U3 = Sharp Dust Sensor [part_number=GP2Y1010AU0F]
  part = Resistor [tolerance=±5% resistance=150 package=THT]
  part_2 = Electrolytic Capacitor [capacitance=220µF voltage=10V package="100 mil [THT, electrolytic]"]

nets:
  N1: Part2.A5(CLK), U3.Vo
  N2: Part2.D12_MISO, U3.LED
  +5V: Part2.+5V, U3.VCC, part.Pin_0
  N3: Part2.GND, U3.LED-GND, U3.S-GND, part_2.-
  N4: U3.V-LED, part.Pin_1, part_2.+

notes:
  GND
  +5V
  Pin 3 - D12
  Pin 6 - +5V
  Pin 5 - A5
  Pin 1 - 5V 150ohm
  Pin 2 - GND
  Pin 4 - GND
  D12 - Pin 3
  A5 - Pin 5
  +
  -

custom parts:
  LCD Keypad Shield: It consists of a 1602 white character blue backlight LCD. The keypad consists of 5 keys — select, up, right, down and left. To save the digital IO pins, the keypad interface uses only one ADC channel. The key value is read through a 5 stage voltage divider.
  Sharp Dust Sensor: Sharp GP2Y1010AU0F Dust Sensor
