# Fritzing sketch keypad-hc-sr04 (saved by Fritzing 0.9.3b)
breadboards: 1

parts:
  hc-sr2 = hc-sr04
  Part3 = LCD Keypad Shield

nets:
  VCC: hc-sr2.VCC, Part3.+5V
  N1: hc-sr2.Trig, Part3.D12_MISO
  N2: hc-sr2.Echo, Part3.D13_SCK
  GND: hc-sr2.GND, Part3.GND

notes:
  D11
  D13
  D3
  D0
  D1
  D2
  D12
  Trig - D12
  Echo - D13

custom parts:
  LCD Keypad Shield: It consists of a 1602 white character blue backlight LCD. The keypad consists of 5 keys — select, up, right, down and left. To save the digital IO pins, the keypad interface uses only one ADC channel. The key value is read through a 5 stage voltage divider.
