# Fritzing sketch keypad_temp_humid (saved by Fritzing 0.9.3b)
breadboards: 1

parts:
  Part2 = LCD Keypad Shield
  Part3 = KY-015 Temperature & Humidity Sensor Module [package="Breakout board"]

nets:
  N1: Part2.D2, Part3.Vin
  N2: Part2.+5V, Part3.-
  N3: Part2.GND, Part3.S

notes:
  DHT11 Sensor Module with LED
  GND
  DATA - D2
  VCC
  D2 - DATA
  D2
  D1
  D0
  D3
  D13
  D12
  D11

custom parts:
  LCD Keypad Shield: It consists of a 1602 white character blue backlight LCD. The keypad consists of 5 keys — select, up, right, down and left. To save the digital IO pins, the keypad interface uses only one ADC channel. The key value is read through a 5 stage voltage divider.
  KY-015 Temperature & Humidity Sensor Module: KY-015 temperature and humidity sensor module, provides a low-latency serial interface to measure humidity and temperature.
