# Fritzing sketch lcd1602 (saved by Fritzing 0.9.3b)

parts:
  LCD1 = LCD screen
  R1 = Resistor [tolerance=±5% resistance=220 package=THT]
  R2 = Trimmer Potentiometer [maximum_resistance=10kΩ package=THT]

nets:
  N1: LCD1.V0, R2.wiper
  N2: LCD1.LED+, R1.Pin_0

notes:
  VSS - LCD GND
  VDD - LCD 전원
  V0 - 글자 대비값
  RS - Register Select 레지스터 설정
  R/W - 읽기/쓰기 모드설정
  E - 쓰기모드 활성화
  LED+
  LED-
  10k 가변저항에 연결
  5V
  13번
  5V 에 220저항
  GND 에 연결. 0 이면 Write 모드
  DB0
  DB1
  DB2
  DB3
  DB5
  DB6
  DB7
  DB4
  DB0 .. DB7 은 LCD 데이터핀
  LCD Data 핀은 4,5,6,7 4개만 써도 됨
  LCD DB4 - 아두이노 D5
  LCD DB5 - 아두이노 D4
  LCD DB6 - 아두이노 D3
  LCD DB7 - 아두이노 D2
