# Fritzing sketch lcd1602_with_dust (saved by Fritzing 0.9.3b)
breadboards: 1

parts:
  Part1 = Arduino Uno (Rev3) - ICSP
  1602 = LCD screen
  R1 = Resistor [tolerance=±5% resistance=220 package=THT]
  R2 = Trimmer Potentiometer [maximum_resistance=10kΩ package=THT]
  U2 = Sharp Dust Sensor [part_number=GP2Y1010AU0F]
  R3 = Resistor [tolerance=±5% resistance=150 package=THT]
  C1 = Electrolytic Capacitor [capacitance=220µF voltage=10V package="100 mil [THT, electrolytic]"]

nets:
  N1: Part1.A5/SCL, U2.Vo
  N2: Part1.D10_PWM/SS, U2.LED
  N3: Part1.D11_PWM/MOSI, 1602.E
  N4: Part1.D12/MISO, 1602.RS
  GND: Part1.GND, 1602.VSS, 1602.R/W, 1602.LED-, R2.leg2, U2.LED-GND, U2.S-GND, C1.-
  N5: Part1.D2, 1602.DB7
  N6: Part1.D3_PWM, 1602.DB6
  N7: Part1.D4, 1602.DB5
  N8: Part1.D5_PWM, 1602.DB4
  5V: Part1.5V, 1602.VDD, R1.Pin_0, R2.leg1, U2.VCC, R3.Pin_0
  N9: 1602.V0, R2.wiper
  N10: 1602.LED+, R1.Pin_1
  N11: U2.V-LED, R3.Pin_1, C1.+

notes:
  DB4  5  6  7
  + - LED
  아두이노 D5  4  3  2
  VSS   V0   R/W
  VDD  RS    E
  아두이노 D12  11
  1 2 3 4 5 6
  1 V-LED --- 5V (150ohm)
  2 LED-GND --- GND (220uf)
  3 LED --- D10
  4 S-GND --- GND
  5 Vo --- A5
  6 Vcc --- 5V

custom parts:
  Sharp Dust Sensor: Sharp GP2Y1010AU0F Dust Sensor
