# Fritzing sketch lcd1602_with_dust_with_led (saved by Fritzing 0.9.3b)
breadboards: 1

parts:
  LCD1602 = LCD screen
  Part1 = Arduino Uno (Rev3) - ICSP
  part = Resistor [tolerance=±5% resistance=220 package=THT]
  U1 = POT [package=pot_mammoth]
  U3 = Sharp Dust Sensor [part_number=GP2Y1010AU0F]
  R4 = Resistor [tolerance=±5% resistance=150 package=THT]
  C2 = Electrolytic Capacitor [capacitance=220µF voltage=10V package="100 mil [THT, electrolytic]"]
  R5 = Resistor [tolerance=±5% resistance=220 package=THT]
  LED3 = smd LED [color="Red (633nm)" package="1206 [SMD]"]

nets:
  VSS: LCD1602.VSS, LCD1602.R/W, LCD1602.LED-, Part1.GND, U1.E, U3.LED-GND, U3.S-GND, C2.-, LED3.cathode
  VDD: LCD1602.VDD, Part1.5V, part.Pin_0, U1.S, U3.VCC, R4.Pin_0
  N1: LCD1602.V0, U1.A
  N2: LCD1602.RS, Part1.ICSP_MISO, Part1.D12/MISO
  N3: LCD1602.E, Part1.D11_PWM/MOSI
  N4: LCD1602.DB4, Part1.D5_PWM
  N5: LCD1602.DB5, Part1.D4
  N6: LCD1602.DB6, Part1.D3_PWM
  N7: LCD1602.DB7, Part1.D2
  N8: LCD1602.LED+, part.Pin_1
  N9: Part1.A5/SCL, U3.Vo
  N10: Part1.D10_PWM/SS, U3.LED
  N11: Part1.D13/SCK, R5.Pin_0
  N12: U3.V-LED, R4.Pin_1, C2.+
  N13: R5.Pin_1, LED3.anode

notes:
  D5,4,3,2 - DBG4,5,6,7
  D12,11 - RS, E
  5V
  10kΩ
  GND
  VSS - GND
  VDD - 5V
  Vo - 10k ohm
  RS - D12
  R/W - GND
  E - D11
  DB4 - D5
  DB5 - D4
  DB6 - D3
  DB7 - D2
  LED (+) - 5V
  LED (-) - GND
  DB4
  DB7
  DB6
  DB5
  1 V-LED --- 5V (150ohm)
  2 LED-GND --- GND (220uf)
  3 LED --- D10
  4 S-GND --- GND
  5 Vo --- A5
  6 Vcc --- 5V
  4 - GND
  3 - D10
  2 - GND
  1 - 5V (150ohm)
  5 - A5
  6 - 5V

custom parts:
  Sharp Dust Sensor: Sharp GP2Y1010AU0F Dust Sensor
